# Fritzing sketch SecureX (saved by Fritzing 0.9.4)
breadboards: 1

parts:
  M1 = STM32407VG Discovery
  OLED_I2C1 = OLED 128x64 I2C Monochrome Display  # not connected
  S2 = Momentary Switch [package=ksa_sealed_tac_switch]
  R1 = Resistor [tolerance=±5% resistance=10k package="2010 [SMD]"]
  S3 = Momentary Switch [package=ksa_sealed_tac_switch]
  R2 = Resistor [tolerance=±5% resistance=10k package="2010 [SMD]"]

nets:
  N1: M1.GND-50, M1.GND-99, R1.Pin_1, R2.Pin_1
  N2: M1.3V-72, M1.3V-97, S2.2, S3.2
  N3: M1.PC7, S2.3, S2.4, R1.Pin_0
  N4: S3.3, R2.Pin_0

custom parts:
  STM32407VG Discovery: The STM32F4DISCOVERY Discovery kit allows users to easily develop applications with the STM32F407VG high performance microcontroller with the ARM® Cortex®-M4 32-bit core. It includes everything required either for beginners or for experienced users to get quickly started.Based on STM32F407VG, it includes an ST-LINK/V2 or ST-LINK/V2-A embedded debug tool, two ST-MEMS digital accelerometers, a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
